# Fritzing sketch WeatherStation (saved by Fritzing 0.9.3b)

parts:
  Componente1 = Adafruit HUZZAH32 ESP32 Feather [part_number="Adafruit #3405"]
  U1 = NodeMCU V1.0
  Part1 = KY-015 Temperature & Humidity Sensor Module [package="Breakout board"]
  Part2 = KY-015 Temperature & Humidity Sensor Module [package="Breakout board"]

nets:
  N1: Componente1.GND, Part1.-
  3.3V: Componente1.3.3V, Part1.Vin
  N2: Componente1.IO12_A11, Part1.S
  N3: U1.D2, Part2.S
  3V3: U1.3V3, Part2.Vin
  N4: U1.GND, Part2.-

notes:
  GPIO 21
  ESP32
  ESP8266
  GPIO04 / D2

custom parts:
  NodeMCU V1.0: ESP8266 based NodeMCU
  KY-015 Temperature & Humidity Sensor Module: KY-015 temperature and humidity sensor module, provides a low-latency serial interface to measure humidity and temperature.
